// Logisim project z8ProcessorSchematic.circ as structural Verilog: 11 circuits, main circuit main
module main (
);

  wire [1:0] cu_1_alu_a_src_sel, cu_1_alu_b_src_sel;
  wire [2:0] cu_1_alu_op;
  wire [7:0] alu_mux_1_alu_in_a, alu_mux_1_alu_in_b;

  CU cu_1 (
    .alu_op(cu_1_alu_op), .alu_a_src_sel(cu_1_alu_a_src_sel), .alu_b_src_sel(cu_1_alu_b_src_sel));  // open: instruction, clk, reset, rf_read_addr_a, rf_read_addr_b
  ALU_MUX alu_mux_1 (
    .alu_src_sel_a(cu_1_alu_a_src_sel), .alu_src_sel_b(cu_1_alu_b_src_sel), .alu_in_a(alu_mux_1_alu_in_a),
    .alu_in_b(alu_mux_1_alu_in_b));  // open: rf_read_data_a, instr_src, rf_read_data_b, mem_read_data
  ALU alu_1 (
    .in_a(alu_mux_1_alu_in_a), .in_b(alu_mux_1_alu_in_b), .alu_op(cu_1_alu_op));  // open: enable, flags_out, alu_out
endmodule

module ALU_op_sel (
  input  enable,
  input  [2:0] op,
  output alu_add,
  output alu_sub,
  output alu_inc,
  output alu_dec,
  output alu_and,
  output alu_or,
  output alu_xor,
  output alu_comp
);

  Decoder #(.select(3)) decoder_1 (
    .out0(alu_add), .out1(alu_sub), .out2(alu_inc), .out3(alu_dec), .out4(alu_and), .out5(alu_or),
    .out6(alu_xor), .out7(alu_comp), .sel(op), .en(enable));
endmodule

module ALU (
  input  [7:0] in_a,
  input  [7:0] in_b,
  input  enable,
  input  [2:0] alu_op,
  output [3:0] flags_out,
  output [7:0] alu_out
);

  wire alu_op_sel_1_alu_add, alu_op_sel_1_alu_sub;
  wire [3:0] alu_add_1_add_flags_out, alu_sub_1_sub_flags_out, bit_extender_1_out, multiplexer_1_out;
  wire [7:0] alu_add_1_add_out, alu_sub_1_sub_out, bit_extender_2_out, multiplexer_2_out;

  ALU_op_sel alu_op_sel_1 (
    .enable(enable), .op(alu_op), .alu_add(alu_op_sel_1_alu_add), .alu_sub(alu_op_sel_1_alu_sub));  // open: alu_inc, alu_dec, alu_and, alu_or, alu_xor, alu_comp
  ALU_add alu_add_1 (
    .enable(alu_op_sel_1_alu_add), .in_a(in_a), .in_b(in_b), .add_out(alu_add_1_add_out),
    .add_flags_out(alu_add_1_add_flags_out));
  ALU_sub alu_sub_1 (
    .enable(alu_op_sel_1_alu_sub), .in_a(in_a), .in_b(in_b), .sub_out(alu_sub_1_sub_out),
    .sub_flags_out(alu_sub_1_sub_flags_out));
  Multiplexer #(.select(3), .width(4)) multiplexer_1 (
    .in0(alu_add_1_add_flags_out), .in1(alu_sub_1_sub_flags_out), .out(multiplexer_1_out), .sel(alu_op));  // open: in2, in3, in4, in5, in6, in7
  Multiplexer #(.select(3), .width(8)) multiplexer_2 (
    .in0(alu_add_1_add_out), .in1(alu_sub_1_sub_out), .out(multiplexer_2_out), .sel(alu_op));  // open: in2, in3, in4, in5, in6, in7
  assign bit_extender_1_out = {{3{enable}}, enable};  // Bit_Extender bit_extender_1
  assign bit_extender_2_out = {{7{enable}}, enable};  // Bit_Extender bit_extender_2
  assign flags_out = multiplexer_1_out & bit_extender_1_out;  // AND_Gate and_1, 4 bits wide
  assign alu_out = multiplexer_2_out & bit_extender_2_out;  // AND_Gate and_2, 8 bits wide
endmodule

module ALU_add (
  input  enable,
  input  [7:0] in_a,
  input  [7:0] in_b,
  output [7:0] add_out,
  output [3:0] add_flags_out
);

  wire comparator_1_eq, xor_1_out, zero_flag_out;
  wire [3:0] not_1_out;
  wire [7:0] adder_1_out, bit_extender_1_out;

  assign bit_extender_1_out = {{7{enable}}, enable};  // Bit_Extender bit_extender_1
  Adder adder_1 (.a(in_a), .b(in_b), .out(adder_1_out), .cout(not_1_out[2]));  // open: cin
  assign add_out = bit_extender_1_out & adder_1_out;  // AND_Gate and_1, 8 bits wide
  Comparator #(.width(1)) comparator_1 (.a(in_a[7]), .b(in_b[7]), .eq(comparator_1_eq));  // open: gt, lt
  or zero_flag (zero_flag_out, add_out[0], add_out[1], add_out[2], add_out[3], add_out[4], add_out[5], add_out[6], add_out[7]);
  xor xor_1 (xor_1_out, add_out[7], in_b[7]);
  not not_1 (not_1_out[0], zero_flag_out);
  and and_2 (not_1_out[3], comparator_1_eq, xor_1_out);
  assign add_flags_out = bit_extender_1_out[7:4] & {not_1_out[3:2], add_out[7], not_1_out[0]};  // AND_Gate and_3, 4 bits wide
endmodule

module ALU_sub (
  input  enable,
  input  [7:0] in_a,
  input  [7:0] in_b,
  output [7:0] sub_out,
  output [3:0] sub_flags_out
);

  wire not_2_out, or_1_out, xor_1_out, xor_2_out;
  wire [6:0] subtractor_1_out;
  wire [7:0] bit_extender_1_out;

  assign bit_extender_1_out = {{7{enable}}, enable};  // Bit_Extender bit_extender_1
  Subtractor subtractor_1 (
    .a(in_a), .b(in_b), .out({sub_flags_out[1], subtractor_1_out}), .bout(sub_flags_out[2]));  // open: bin
  xor xor_1 (xor_1_out, in_a[7], in_b[7]);
  assign sub_out = bit_extender_1_out & {sub_flags_out[1], subtractor_1_out};  // AND_Gate and_1, 8 bits wide
  xor xor_2 (xor_2_out, sub_flags_out[1], in_b[7]);
  or or_1 (or_1_out, subtractor_1_out[0], subtractor_1_out[1], subtractor_1_out[2], subtractor_1_out[3], subtractor_1_out[4], subtractor_1_out[5], subtractor_1_out[6], sub_flags_out[1]);
  not not_1 (sub_flags_out[0], or_1_out);
  not not_2 (not_2_out, xor_2_out);
  and and_2 (sub_flags_out[3], not_2_out, xor_1_out);
endmodule

module ALU_MUX (
  input  [7:0] rf_read_data_a,
  input  [1:0] alu_src_sel_a,
  input  [7:0] instr_src,
  input  [7:0] rf_read_data_b,
  input  [7:0] mem_read_data,
  input  [1:0] alu_src_sel_b,
  output [7:0] alu_in_a,
  output [7:0] alu_in_b
);

  Multiplexer #(.select(2), .width(8)) multiplexer_1 (
    .in1(rf_read_data_a), .out(alu_in_a), .sel(alu_src_sel_a));  // open: in0, in2, in3
  Multiplexer #(.select(2), .width(8)) multiplexer_2 (
    .in0(instr_src), .in1(rf_read_data_b), .in2(mem_read_data), .out(alu_in_b), .sel(alu_src_sel_b));  // open: in3
endmodule

module CU_MUX (
  input  [23:0] instruction,
  output [7:0] opcode,
  output [7:0] dest,
  output [7:0] source,
  output NOP,
  output LDM,
  output LDR,
  output LDD,
  output STR,
  output STD,
  output ADR,
  output ADD,
  output SBR,
  output SBD
);

  Demultiplexer #(.select(5)) demultiplexer_1 (
    .out0(NOP), .out1(LDM), .out2(LDR), .out3(LDD), .out4(STR), .out5(STD), .out6(ADR), .out7(ADD),
    .out8(SBR), .out9(SBD), .in(1'b1), .sel(instruction[20:16]));  // open: out10, out11, out12, out13, out14, out15, out16, out17, out18, out19, out20, out21, out22, out23, out24, out25, out26, out27, out28, out29, out30, out31

  assign dest = instruction[15:8];
  assign opcode = instruction[23:16];
  assign source = instruction[7:0];
endmodule

module CU_ADD (
  input  [7:0] dest,
  input  enable,
  output [7:0] rf_read_addr_a
);

  wire [7:0] bit_extender_1_out;

  assign bit_extender_1_out = {{7{enable}}, enable};  // Bit_Extender bit_extender_1
  assign rf_read_addr_a = dest & bit_extender_1_out;  // AND_Gate and_1, 8 bits wide
endmodule

module CU (
  input  [23:0] instruction,
  input  clk,
  input  reset,
  output [7:0] rf_read_addr_a,
  output [7:0] rf_read_addr_b,
  output [2:0] alu_op,
  output [1:0] alu_a_src_sel,
  output [1:0] alu_b_src_sel
);

  wire comparator_1_eq, cu_mux_1_add, cu_mux_1_adr, cu_mux_1_ldd, cu_mux_1_ldr;
  wire [1:0] adder_1_out, state_q;
  wire [2:0] cu_adr_1_alu_op;
  wire [7:0] bit_extender_1_out, cu_add_1_rf_read_addr_a, cu_adr_1_rf_read_addr_a, cu_adr_1_rf_read_addr_b,
       cu_ldr_1_rf_read_addr_b, cu_mux_1_dest, cu_mux_1_source, read_addr_a_out, read_addr_b_out;

  Register #(.width(2)) state (.D(adder_1_out), .clk(clk), .Q(state_q), .clr(reset));  // open: en
  CU_MUX cu_mux_1 (
    .instruction(instruction), .dest(cu_mux_1_dest), .source(cu_mux_1_source), .LDR(cu_mux_1_ldr),
    .LDD(cu_mux_1_ldd), .ADR(cu_mux_1_adr), .ADD(cu_mux_1_add));  // open: opcode, NOP, LDM, STR, STD, SBR, SBD
  Adder #(.width(2)) adder_1 (.a(2'b01), .b(state_q), .out(adder_1_out));  // open: cin, cout
  CU_LDR cu_ldr_1 (.src(cu_mux_1_source), .enable(cu_mux_1_ldr), .rf_read_addr_b(cu_ldr_1_rf_read_addr_b));
  CU_ADR cu_adr_1 (
    .dest(cu_mux_1_dest), .source(cu_mux_1_source), .enable(cu_mux_1_adr),
    .rf_read_addr_a(cu_adr_1_rf_read_addr_a), .rf_read_addr_b(cu_adr_1_rf_read_addr_b),
    .alu_op(cu_adr_1_alu_op));  // open: alu_a_src_sel, alu_b_src_sel
  CU_ADD cu_add_1 (.dest(cu_mux_1_dest), .enable(cu_mux_1_add), .rf_read_addr_a(cu_add_1_rf_read_addr_a));
  Comparator #(.width(2)) comparator_1 (.a(state_q), .b(2'b01), .eq(comparator_1_eq));  // open: gt, lt
  assign read_addr_b_out = cu_adr_1_rf_read_addr_b | cu_ldr_1_rf_read_addr_b;  // OR_Gate read_addr_b, 8 bits wide
  assign read_addr_a_out = cu_adr_1_rf_read_addr_a | cu_add_1_rf_read_addr_a;  // OR_Gate read_addr_a, 8 bits wide
  assign bit_extender_1_out = {{7{comparator_1_eq}}, comparator_1_eq};  // Bit_Extender bit_extender_1
  assign rf_read_addr_b = read_addr_b_out & bit_extender_1_out;  // AND_Gate and_1, 8 bits wide
  assign rf_read_addr_a = read_addr_a_out & bit_extender_1_out;  // AND_Gate and_2, 8 bits wide
  assign alu_op = cu_adr_1_alu_op;  // OR_Gate alu_ops, 3 bits wide OR_Gate

  // Notes on the sheet:
  //   decode
  //   execute
endmodule

module CU_ADR (
  input  [7:0] dest,
  input  [7:0] source,
  input  enable,
  output [7:0] rf_read_addr_a,
  output [7:0] rf_read_addr_b,
  output [2:0] alu_op,
  output [1:0] alu_a_src_sel,
  output [1:0] alu_b_src_sel
);

  wire [7:0] bit_extender_1_out;

  assign bit_extender_1_out = {{7{enable}}, enable};  // Bit_Extender bit_extender_1
  assign rf_read_addr_a = dest & bit_extender_1_out;  // AND_Gate and_1, 8 bits wide
  assign rf_read_addr_b = source & bit_extender_1_out;  // AND_Gate and_2, 8 bits wide

  assign alu_a_src_sel = 2'b11;
  assign alu_b_src_sel = 2'b11;
  assign alu_op = 3'b001;
endmodule

module CU_LDR (
  input  [7:0] src,
  input  enable,
  output [7:0] rf_read_addr_b
);

  wire [7:0] bit_extender_1_out;

  assign bit_extender_1_out = {{7{enable}}, enable};  // Bit_Extender bit_extender_1
  assign rf_read_addr_b = src & bit_extender_1_out;  // AND_Gate and_1, 8 bits wide
endmodule
